# Fritzing sketch Magic8Ball (saved by Fritzing 0.9.3b)

parts:
  M1 = DOIT Esp32 DevKit v1 (30 pins long, 11 pins width) [part_number=ESP32S-PIN30]
  DFPlayer_Mini1 = DFPlayer MINI [package="DIP (Dual Inline) [THT]"]
  S1 = Round Pushbutton
  GY1 = MPU-6050 Board GY-521 [form="♀ (female)" package=THT]
  J1 = Piezo Speaker
  VCC1 = 4 x AAA Battery Mount  # not connected
  Part1 = Adafruit Mini TFT Display - 0.96in 160x80 [part_number="Adafruit 3533"]

nets:
  3V3: M1.3V3, DFPlayer_Mini1.VCC, GY1.pin1, Part1.SDCS
  GND: M1.GND, DFPlayer_Mini1.GND, GY1.pin2, Part1.BACKLIGHT
  N1: M1.D2, Part1.TFTCS
  N2: M1.D4, Part1.MOSI
  N3: M1.RX2, DFPlayer_Mini1.TX
  N4: M1.TX2, DFPlayer_Mini1.RX
  N5: M1.D18, Part1.DC
  N6: M1.D21, GY1.pin4
  N7: M1.D22, GY1.pin3
  N8: M1.D23, Part1.TFTRST
  N9: M1.D14, Part1.SDA
  N10: M1.VIN, S1.leg1
  N11: DFPlayer_Mini1.SPK1, J1.pin2
  N12: DFPlayer_Mini1.SPK2, J1.pin1

custom parts:
  DOIT Esp32 DevKit v1 (30 pins long, 11 pins width): The DOIT Esp32 DevKit v1 is one of the development board created by DOIT to evaluate the ESP-WROOM-32 module. It is based on the ESP32 microcontroller that boasts Wifi, Bluetooth, Ethernet and Low Power support all in a single chip. (vanepp) made breadboard work, adjusted pin numbering and labels and reduced size of schematic and cleaned up pcb. This chip is 30pins long (2 x15) and 11 pins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
  DFPlayer MINI: MP3 module by DFRobot.com for playing Music from an SD-Card. Supports WAV and MP3 files.
  MPU-6050 Board GY-521: Acelerometro y Giroscopio MPU-6050 Board GY-521
  Adafruit Mini TFT Display - 0.96in 160x80: It's the size of your thumbnail, with glorious 160x80 pixel color... it's the Adafruit Mini TFT Breakout! This very very small display is only 0.96" diagonal, packed with RGB pixels, for making very small high-density displays. The display uses 4-wire SPI to communicate and has its own pixel-addressable frame buffer, it can be used with every kind of microcontroller. Even a very small one with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
